# Fritzing sketch breadboard (saved by Fritzing 0.9.3b)
breadboards: 6

parts:
  Microcontroller = IC, DIP package, 40 pins [chip_label="Atmega 162"]
  RESET = Pushbutton [package="[SMD]"]
  LED = LED - 3mm [color="Red (633nm)" package="3 mm [THT]"]
  VCC1 = Battery block 9V
  C3 = Capacitor [package=cap-pth-small]
  U1 = Voltage Regulator - 5V [package="TO220 [THT]"]
  C2 = Capacitor [package=cap-pth-large]
  Clock = Crystal [frequency="4 MHz" package=THT]
  UART_transceiver = IC, DIP package, 20 pins [chip_label=MAX233]  # not connected

nets:
  N1: Microcontroller.pin1, LED.anode
  N2: Microcontroller.pin3, Microcontroller.pin9, RESET.Pin_1, RESET.Pin_2
  N3: Microcontroller.pin18, Clock.pin_1
  N4: Microcontroller.pin19, Clock.pin_0
  GND: Microcontroller.pin20, RESET.Pin_3, RESET.Pin_4, LED.cathode, VCC1.-, C3.2, U1.GND, C2.2
  5V: Microcontroller.pin40, U1.output_voltage, C2.1
  N5: VCC1.+, C3.1, U1.input_voltage
